// Logisim project LC-2200-16.circ as structural Verilog
module LC2200_Datapath (
);

  wire CLK, DrALU, DrMEM, DrOFF, DrPC, DrREG, LdA, LdB, LdIR, LdMAR, LdPC, nor_1_out, WrMEM, WrREG, Z;
  wire [1:0] CC, func;
  wire [2:0] OP;
  wire [3:0] regno, RX, RY;
  wire [3:1] RZ;
  wire [15:0] A_q, ALU_out, B_q, bit_extender_1_out, controlled_buffer_1_out, MAR_q, PC_q, RAM_dout,
       Registers_dout;

  // Probe on controlled_buffer_1_out
  Register #(.width(16)) PC (.D(controlled_buffer_1_out), .en(LdPC), .Q(PC_q), .clk(CLK));  // open: clr
  assign controlled_buffer_1_out = DrPC ? PC_q : 16'bz;  // Controlled_Buffer controlled_buffer_1
  nor nor_1 (nor_1_out, controlled_buffer_1_out[15], controlled_buffer_1_out[14], controlled_buffer_1_out[13], controlled_buffer_1_out[12], controlled_buffer_1_out[11], controlled_buffer_1_out[10], controlled_buffer_1_out[9], controlled_buffer_1_out[8], controlled_buffer_1_out[7], controlled_buffer_1_out[6], controlled_buffer_1_out[5], controlled_buffer_1_out[4], controlled_buffer_1_out[3], controlled_buffer_1_out[2], controlled_buffer_1_out[1], controlled_buffer_1_out[0]);
  Register #(.width(16)) A (.D(controlled_buffer_1_out), .en(LdA), .Q(A_q), .clk(CLK));  // open: clr
  Register #(.width(1)) u_Z (.D(nor_1_out), .Q(Z));  // open: en, clk, clr
  ALU ALU (.func(func), .A(A_q), .B(B_q), .OUT(ALU_out));
  assign controlled_buffer_1_out = DrALU ? ALU_out : 16'bz;  // Controlled_Buffer controlled_buffer_2
  Register #(.width(16)) B (.D(controlled_buffer_1_out), .en(LdB), .Q(B_q), .clk(CLK));  // open: clr
  Registers Registers (.WrREG(WrREG), .regno(regno), .CLK(CLK), .Din(controlled_buffer_1_out), .Dout(Registers_dout));
  assign controlled_buffer_1_out = DrREG ? Registers_dout : 16'bz;  // Controlled_Buffer controlled_buffer_3
  Register #(.width(16)) MAR (.D(controlled_buffer_1_out), .en(LdMAR), .Q(MAR_q), .clk(CLK));  // open: clr
  RAM RAM (.WrMEM(WrMEM), .CLK(CLK), .Addr(MAR_q), .Din(controlled_buffer_1_out), .Dout(RAM_dout));
  assign controlled_buffer_1_out = DrMEM ? RAM_dout : 16'bz;  // Controlled_Buffer controlled_buffer_4
  Register #(.width(16)) IR (.D(controlled_buffer_1_out), .en(LdIR), .Q({OP, RX, RY, RZ, CC}), .clk(CLK));  // open: clr
  assign bit_extender_1_out = {{11{RZ[3]}}, {RZ, CC}};  // Bit_Extender bit_extender_1
  assign controlled_buffer_1_out = DrOFF ? bit_extender_1_out : 16'bz;  // Controlled_Buffer controlled_buffer_5

  // Other names for the same wires on the sheet: RZ[0] = CC[1]
endmodule

module ALU (
  input  [15:0] A,
  input  [15:0] B,
  input  [1:0] func,
  output [15:0] OUT
);

  wire [15:0] ADD, NAND, plus_1, SUB;

  Adder #(.width(16)) adder_1 (.a(A), .b(B), .out(ADD));  // open: cin, cout
  Subtractor #(.width(16)) subtractor_1 (.a(A), .b(B), .out(SUB));  // open: bin, bout
  Multiplexer #(.select(2), .width(16), .disabled(0), .enable("false")) multiplexer_1 (
    .in0(ADD), .in1(NAND), .in2(SUB), .in3(plus_1), .out(OUT), .sel(func));
  assign NAND = ~(A & B);  // NAND_Gate nand_1, 16 bits wide
  Adder #(.width(16)) adder_2 (.a(A), .b(16'h1), .out(plus_1));  // open: cin, cout
endmodule

module Registers (
  input  [15:0] Din,
  input  WrREG,
  input  [3:0] regno,
  input  CLK,
  output [15:0] Dout
);

  wire demultiplexer_1_out1, demultiplexer_1_out2, demultiplexer_1_out3, demultiplexer_1_out4,
       demultiplexer_1_out5, demultiplexer_1_out6, demultiplexer_1_out7, demultiplexer_1_out8,
       demultiplexer_1_out9, demultiplexer_1_out10, demultiplexer_1_out11, demultiplexer_1_out12,
       demultiplexer_1_out13, demultiplexer_1_out14, demultiplexer_1_out15;
  wire [15:0] register_1_q, register_2_q, register_3_q, register_4_q, register_5_q, register_6_q,
       register_7_q, register_8_q, register_9_q, register_10_q, register_11_q, register_12_q, register_13_q,
       register_14_q, register_15_q;

  Demultiplexer #(.select(4), .disabled(0), .enable("false")) demultiplexer_1 (
    .out1(demultiplexer_1_out1), .out2(demultiplexer_1_out2), .out3(demultiplexer_1_out3),
    .out4(demultiplexer_1_out4), .out5(demultiplexer_1_out5), .out6(demultiplexer_1_out6),
    .out7(demultiplexer_1_out7), .out8(demultiplexer_1_out8), .out9(demultiplexer_1_out9),
    .out10(demultiplexer_1_out10), .out11(demultiplexer_1_out11), .out12(demultiplexer_1_out12),
    .out13(demultiplexer_1_out13), .out14(demultiplexer_1_out14), .out15(demultiplexer_1_out15), .in(WrREG),
    .sel(regno));  // open: out0
  Register #(.width(16)) register_1 (.D(Din), .en(demultiplexer_1_out4), .Q(register_1_q), .clk(CLK));  // open: clr
  Register #(.width(16)) register_2 (.D(Din), .en(demultiplexer_1_out8), .Q(register_2_q), .clk(CLK));  // open: clr
  Register #(.width(16)) register_3 (.D(Din), .en(demultiplexer_1_out12), .Q(register_3_q), .clk(CLK));  // open: clr
  Register #(.width(16)) register_4 (.D(Din), .en(demultiplexer_1_out1), .Q(register_4_q), .clk(CLK));  // open: clr
  Register #(.width(16)) register_5 (.D(Din), .en(demultiplexer_1_out5), .Q(register_5_q), .clk(CLK));  // open: clr
  Register #(.width(16)) register_6 (.D(Din), .en(demultiplexer_1_out9), .Q(register_6_q), .clk(CLK));  // open: clr
  Register #(.width(16)) register_7 (.D(Din), .en(demultiplexer_1_out13), .Q(register_7_q), .clk(CLK));  // open: clr
  Register #(.width(16)) register_8 (.D(Din), .en(demultiplexer_1_out2), .Q(register_8_q), .clk(CLK));  // open: clr
  Register #(.width(16)) register_9 (.D(Din), .en(demultiplexer_1_out6), .Q(register_9_q), .clk(CLK));  // open: clr
  Register #(.width(16)) register_10 (.D(Din), .en(demultiplexer_1_out10), .Q(register_10_q), .clk(CLK));  // open: clr
  Register #(.width(16)) register_11 (.D(Din), .en(demultiplexer_1_out14), .Q(register_11_q), .clk(CLK));  // open: clr
  Register #(.width(16)) register_12 (.D(Din), .en(demultiplexer_1_out3), .Q(register_12_q), .clk(CLK));  // open: clr
  Register #(.width(16)) register_13 (.D(Din), .en(demultiplexer_1_out7), .Q(register_13_q), .clk(CLK));  // open: clr
  Register #(.width(16)) register_14 (.D(Din), .en(demultiplexer_1_out11), .Q(register_14_q), .clk(CLK));  // open: clr
  Register #(.width(16)) register_15 (.D(Din), .en(demultiplexer_1_out15), .Q(register_15_q), .clk(CLK));  // open: clr
  Multiplexer #(.select(4), .width(16), .disabled(0), .enable("false")) multiplexer_1 (
    .in0({16{1'b0}}), .in1(register_4_q), .in2(register_8_q), .in3(register_12_q), .in4(register_1_q),
    .in5(register_5_q), .in6(register_9_q), .in7(register_13_q), .in8(register_2_q), .in9(register_6_q),
    .in10(register_10_q), .in11(register_14_q), .in12(register_3_q), .in13(register_7_q),
    .in14(register_11_q), .in15(register_15_q), .out(Dout), .sel(regno));
endmodule

module RAM (
  input  [15:0] Addr,
  input  [15:0] Din,
  input  WrMEM,
  input  CLK,
  output [15:0] Dout
);

  wire not_1_out;

  RAM_part #(.addrWidth(16), .dataWidth(16)) ram_1 (
    .addr(Addr), .data(Dout), .clk(CLK), .ld(not_1_out));  // open: sel, clr
  not not_1 (not_1_out, WrMEM);
  assign Dout = WrMEM ? Din : 16'bz;  // Controlled_Buffer controlled_buffer_1
endmodule
